# Fritzing sketch multiplexing (saved by Fritzing 0.9.0b)
breadboards: 2

parts:
  U1 = 74HC4051 [package=so16]
  U2 = 74HC4051 [package=so16]
  U3 = POT [package=alps_pot]
  U4 = POT [package=alps_pot]
  U5 = POT [package=alps_pot]
  U6 = POT [package=alps_pot]
  U7 = POT [package=alps_pot]
  U8 = POT [package=alps_pot]
  U9 = POT [package=alps_pot]
  U10 = POT [package=alps_pot]
  U12 = POT [package=alps_pot]
  U15 = POT [package=alps_pot]
  U17 = POT [package=alps_pot]
  U18 = POT [package=alps_pot]
  Part2 = Arduino Mega ADK (Rev3)
  Power_plug1 = Power plug
  U21 = 74HC595 [package="DIP16 [THT]"]
  D1 = LED_BARGRAPH_10 [package=led_bargaph_10]
  U22 = 74HC595 [package="DIP16 [THT]"]
  U23 = 74HC595 [package="DIP16 [THT]"]
  U24 = 74HC595 [package="DIP16 [THT]"]
  U25 = 74HC595 [package="DIP16 [THT]"]
  U26 = 74HC595 [package="DIP16 [THT]"]
  D2 = LED_BARGRAPH_10 [package=led_bargaph_10]  # not connected
  D3 = LED_BARGRAPH_10 [package=led_bargaph_10]  # not connected
  D4 = LED_BARGRAPH_10 [package=led_bargaph_10]  # not connected
  D5 = LED_BARGRAPH_10 [package=led_bargaph_10]  # not connected
  D6 = LED_BARGRAPH_10 [package=led_bargaph_10]  # not connected

nets:
  N1: U1.IO4, U8.S
  N2: U1.IO6, U7.S
  N3: U1.IO, Part2.A2
  N4: U1.IO7, U10.S
  N5: U1.IO5, U9.S
  GND: U1.INH, U1.VEE, U1.VSS, U2.INH, U2.VEE, U2.VSS, U3.A, U4.A, U5.A, U6.A, U7.A, U8.A, U9.A, U10.A, U12.A, U15.A, U17.A, U18.A, Part2.GND, Power_plug1.GND, U21.GND, U21.OE, D1.A_A, D1.B_A, D1.C_A, D1.D_A, D1.E_A, D1.F_A, D1.G_A, D1.H_A, D1.I_A, D1.J_A, U22.GND, U22.OE, U23.GND, U23.OE, U24.GND, U24.OE, U25.GND, U25.OE, U26.GND, U26.OE
  N6: U1.C, U2.C, Part2.D4_PWM
  N7: U1.B, U2.B, Part2.D3_PWM
  N8: U1.A, U2.A, Part2.D2_PWM
  N9: U1.IO3, U5.S
  N10: U1.IO0, U3.S
  N11: U1.IO1, U4.S
  N12: U1.IO2, U6.S
  VDD: U1.VDD, U2.VDD, U3.E, U4.E, U5.E, U6.E, U7.E, U8.E, U9.E, U10.E, U12.E, U15.E, U17.E, U18.E, Part2.5V
  N13: U2.IO, Part2.A3
  N14: U2.IO3, U17.S
  N15: U2.IO0, U15.S
  N16: U2.IO1, U18.S
  N17: U2.IO2, U12.S
  N18: Part2.D12_PWM, U21.SH_CP, U22.SH_CP, U23.SH_CP, U24.SH_CP, U25.SH_CP, U26.SH_CP
  N19: Part2.D11_PWM, U21.DS
  N20: Part2.D8_PWM, U21.ST_CP, U22.ST_CP, U23.ST_CP, U24.ST_CP, U25.ST_CP, U26.ST_CP
  VCC: Power_plug1.VCC, U21.MR, U21.VCC, U22.MR, U22.VCC, U23.MR, U23.VCC, U24.MR, U24.VCC, U25.MR, U25.VCC, U26.MR, U26.VCC
  N21: U21.Q1, D1.I_C
  N22: U21.Q2, D1.H_C
  N23: U21.Q3, D1.G_C, D1.F_C
  N24: U21.Q4, D1.D_C
  N25: U21.Q5, D1.C_C
  N26: U21.Q6, D1.B_C
  N27: U21.Q7, D1.A_C
  N28: U21.Q7', U22.DS
  N29: U21.Q0, D1.J_C
  N30: U22.Q7', U23.DS
  N31: U23.Q7', U24.DS
  N32: U24.Q7', U25.DS
  N33: U25.Q7', U26.DS
